# Fritzing sketch Resistive Touchscreen (saved by Fritzing 0.9.4)

parts:
  Part1 = Arduino Nano (Rev3.0)
  J1 = female pin header, 5 pins [form="♀ (female)"]

nets:
  N1: Part1.D2, J1.pin5
  N2: Part1.D3, J1.pin4
  N3: Part1.D4, J1.pin2
  N4: Part1.D5, J1.pin1
  N5: Part1.A0, J1.pin3

notes:
  Elo E212465 15" Touch Screen
